// Logisim project Michael.circ as structural Verilog: 12 circuits, main circuit main
module main (
);

  wire clock_1_out, ex_mem_1_regwriteout, execute_1_regwriteout, memory_1_regwriteout;
  wire [4:0] ex_mem_1_rwout, execute_1_rwout, forwards_hazards_1_sa, memory_1_rwout;
  wire [31:0] ex_mem_1_alures_out, ex_mem_1_pcout, execute_1_aluoutput, execute_1_pcout,
       forwards_hazards_1_aout, forwards_hazards_1_bout, memory_1_alures_out, memory_1_pcout;

  Forwards_Hazards forwards_hazards_1 (
    .Aout(forwards_hazards_1_aout), .Bout(forwards_hazards_1_bout), .Sa(forwards_hazards_1_sa));  // open: ALUSrc, PC, A, B, WriteBack_Data, Memory_Data, RType, rs1, rs2, rd_EX, rd_MEM, lw_EX, lw_MEM, Imm32, ImmU, UI, LUI
  Clock clock_1 (.out(clock_1_out));
  Execute execute_1 (
    .A(forwards_hazards_1_aout), .B(forwards_hazards_1_bout), .Sa(forwards_hazards_1_sa),
    .ALUoutput(execute_1_aluoutput), .RegWriteOut(execute_1_regwriteout), .rWout(execute_1_rwout),
    .PCout(execute_1_pcout));  // open: Funct30, Op, RegWriteIn, rW, PC
  EX_MEM ex_mem_1 (
    .ALUres_in(execute_1_aluoutput), .RegWrite(execute_1_regwriteout), .rW(execute_1_rwout),
    .PC(execute_1_pcout), .clock(clock_1_out), .ALUres_out(ex_mem_1_alures_out),
    .RegWriteOut(ex_mem_1_regwriteout), .rWout(ex_mem_1_rwout), .PCout(ex_mem_1_pcout));
  Memory memory_1 (
    .ALUres_in(ex_mem_1_alures_out), .RegWriteIn(ex_mem_1_regwriteout), .rW(ex_mem_1_rwout),
    .PC(ex_mem_1_pcout), .ALUres_out(memory_1_alures_out), .RegWriteOut(memory_1_regwriteout),
    .rWout(memory_1_rwout), .PCout(memory_1_pcout));
  MEM_WB mem_wb_1 (
    .ALUres_in(memory_1_alures_out), .RegWriteIn(memory_1_regwriteout), .rW(memory_1_rwout),
    .PC(memory_1_pcout), .clock(clock_1_out));  // open: ALUres_out, RegWriteOut, rWout, PCout
endmodule

module Execute (
  input  [31:0] A,
  input  [31:0] B,
  input  Funct30,
  input  [4:0] Sa,
  input  [3:0] Op,
  input  RegWriteIn,
  input  [4:0] rW,
  input  [31:0] PC,
  output [31:0] ALUoutput,
  output RegWriteOut,
  output [4:0] rWout,
  output [31:0] PCout
);

  wire [31:0] alu_1_p6;

  // ALU alu_1: pin names not known; wires that end beside it: Funct30, A, B, Op, Sa, alu_1_p6
  ALUresult aluresult_1 (
    .A(A), .B(B), .C(alu_1_p6), .Funct30(Funct30), .Op0(Op[0]), .Op1(Op[1]), .RegWriteIn(RegWriteIn),
    .ALUoutput(ALUoutput), .RegWriteOut(RegWriteOut));

  assign PCout = PC;
  assign rWout = rW;
endmodule

module ALUresult (
  input  [31:0] A,
  input  [31:0] B,
  input  [31:0] C,
  input  Funct30,
  input  Op0,
  input  Op1,
  input  RegWriteIn,
  output [31:0] ALUoutput,
  output RegWriteOut
);

  wire comparator_1_lt, comparator_2_lt;
  wire [31:0] bit_extender_1_out, bit_extender_2_out, multiplexer_1_out, multiplexer_2_out;

  Comparator #(.width(32)) comparator_1 (.a(A), .b(B), .lt(comparator_1_lt));  // open: gt, eq
  Comparator #(.width(32), .mode("unsigned")) comparator_2 (.a(A), .b(B), .lt(comparator_2_lt));  // open: gt, eq
  assign bit_extender_1_out = {{31{1'b0}}, comparator_1_lt};  // Bit_Extender bit_extender_1
  assign bit_extender_2_out = {{31{1'b0}}, comparator_2_lt};  // Bit_Extender bit_extender_2
  Multiplexer #(.width(32), .enable("false")) multiplexer_1 (
    .in0(bit_extender_1_out), .in1(bit_extender_2_out), .out(multiplexer_1_out), .sel(Funct30));
  Multiplexer #(.width(32), .enable("false")) multiplexer_2 (
    .in0(multiplexer_1_out), .in1(C), .out(multiplexer_2_out), .sel(Op0));
  Multiplexer #(.width(32), .enable("false")) multiplexer_3 (
    .in0(multiplexer_2_out), .in1(C), .out(ALUoutput), .sel(Op1));

  assign RegWriteOut = RegWriteIn;
endmodule

module EX_MEM (
  input  [31:0] ALUres_in,
  input  RegWrite,
  input  [4:0] rW,
  input  [31:0] PC,
  input  clock,
  output [31:0] ALUres_out,
  output RegWriteOut,
  output [4:0] rWout,
  output [31:0] PCout
);

  Register #(.width(32)) register_1 (.D(ALUres_in), .clk(clock), .Q(ALUres_out));  // open: en, clr
  Register #(.width(1)) register_2 (.D(RegWrite), .clk(clock), .Q(RegWriteOut));  // open: en, clr
  Register #(.width(5)) register_3 (.D(rW), .clk(clock), .Q(rWout));  // open: en, clr
  Register #(.width(32)) register_4 (.D(PC), .clk(clock), .Q(PCout));  // open: en, clr
endmodule

module Memory (
  input  [31:0] ALUres_in,
  input  RegWriteIn,
  input  [4:0] rW,
  input  [31:0] PC,
  output [31:0] ALUres_out,
  output RegWriteOut,
  output [4:0] rWout,
  output [31:0] PCout
);


  assign ALUres_out = ALUres_in;
  assign PCout = PC;
  assign RegWriteOut = RegWriteIn;
  assign rWout = rW;
endmodule

module MEM_WB (
  input  [31:0] ALUres_in,
  input  RegWriteIn,
  input  [4:0] rW,
  input  [31:0] PC,
  input  clock,
  output [31:0] ALUres_out,
  output RegWriteOut,
  output [4:0] rWout,
  output [31:0] PCout
);

  Register #(.width(32)) register_1 (.D(ALUres_in), .clk(clock), .Q(ALUres_out));  // open: en, clr
  Register #(.width(1)) register_2 (.D(RegWriteIn), .clk(clock), .Q(RegWriteOut));  // open: en, clr
  Register #(.width(5)) register_3 (.D(rW), .clk(clock), .Q(rWout));  // open: en, clr
  Register #(.width(32)) register_4 (.D(PC), .clk(clock), .Q(PCout));  // open: en, clr
endmodule

module Forwards_Hazards (
  input  ALUSrc,
  input  [31:0] PC,
  input  [31:0] A,
  input  [31:0] B,
  input  [31:0] WriteBack_Data,
  input  [31:0] Memory_Data,
  input  RType,
  input  [4:0] rs1,
  input  [4:0] rs2,
  input  [4:0] rd_EX,
  input  [4:0] rd_MEM,
  input  lw_EX,
  input  lw_MEM,
  input  [31:0] Imm32,
  input  [19:0] ImmU,
  input  UI,
  input  LUI,
  output [31:0] Aout,
  output [31:0] Bout,
  output [4:0] Sa
);

  wire hazarddetectionunit_1_rs1_rdex_ex, hazarddetectionunit_1_rs1_rdmem_mem,
       hazarddetectionunit_1_rs2_rd2mem_mem, hazarddetectionunit_1_rs2_rdex_ex;
  wire [4:0] forwardunit_1_bout;
  wire [31:0] forwardunit_1_aout;
  wire [31:5] forwardunit_1_bout_2;

  HazardDetectionUnit hazarddetectionunit_1 (
    .rs1(rs1), .rs2(rs2), .rd_EX(rd_EX), .rd_MEM(rd_MEM), .LW_EX(lw_EX), .LW_MEM(lw_MEM), .RType(RType),
    .rs1_rdEX_EX(hazarddetectionunit_1_rs1_rdex_ex), .rs1_rdMEM_MEM(hazarddetectionunit_1_rs1_rdmem_mem),
    .rs2_rdEX_EX(hazarddetectionunit_1_rs2_rdex_ex), .rs2_rd2MEM_MEM(hazarddetectionunit_1_rs2_rd2mem_mem));
  ForwardUnit forwardunit_1 (
    .A(A), .B(B), .WriteBack_Data(WriteBack_Data), .Memory_Data(Memory_Data),
    .rs1_rdMEM_MEM(hazarddetectionunit_1_rs1_rdmem_mem),
    .rs2_rdMEM_MEM(hazarddetectionunit_1_rs2_rd2mem_mem), .rs1_rdEX_EX(hazarddetectionunit_1_rs1_rdex_ex),
    .rs2_rdEX_EX(hazarddetectionunit_1_rs2_rdex_ex), .Aout(forwardunit_1_aout),
    .Bout({forwardunit_1_bout_2, forwardunit_1_bout}));
  ALUinput_selection aluinput_selection_1 (
    .ALUSrc(ALUSrc), .B({forwardunit_1_bout_2, forwardunit_1_bout}), .Immediate(Imm32), .immU(ImmU), .UI(UI),
    .A(forwardunit_1_aout), .PC(PC), .Sa_in(Imm32[4:0]), .rs2_Data(forwardunit_1_bout), .Shift(RType),
    .LUI(LUI), .Bout(Bout), .Aout(Aout), .Sa_out(Sa));
endmodule

module ForwardUnit (
  input  [31:0] A,
  input  [31:0] B,
  input  [31:0] WriteBack_Data,
  input  [31:0] Memory_Data,
  input  rs1_rdMEM_MEM,
  input  rs2_rdMEM_MEM,
  input  rs1_rdEX_EX,
  input  rs2_rdEX_EX,
  output [31:0] Aout,
  output [31:0] Bout
);

  wire [31:0] multiplexer_1_out, multiplexer_2_out;

  Multiplexer #(.width(32), .enable("false")) multiplexer_1 (
    .in0(A), .in1(Memory_Data), .out(multiplexer_1_out), .sel(rs1_rdMEM_MEM));
  Multiplexer #(.width(32), .enable("false")) multiplexer_2 (
    .in0(B), .in1(Memory_Data), .out(multiplexer_2_out), .sel(rs2_rdMEM_MEM));
  Multiplexer #(.width(32), .enable("false")) multiplexer_3 (
    .in0(multiplexer_1_out), .in1(WriteBack_Data), .out(Aout), .sel(rs1_rdEX_EX));
  Multiplexer #(.width(32), .enable("false")) multiplexer_4 (
    .in0(multiplexer_2_out), .in1(WriteBack_Data), .out(Bout), .sel(rs2_rdEX_EX));
endmodule

module HazardDetectionUnit (
  input  [4:0] rs1,
  input  [4:0] rs2,
  input  [4:0] rd_EX,
  input  [4:0] rd_MEM,
  input  LW_EX,
  input  LW_MEM,
  input  RType,
  output rs1_rdEX_EX,
  output rs1_rdMEM_MEM,
  output rs2_rdEX_EX,
  output rs2_rd2MEM_MEM
);

  wire equality_1_equality_out, equality_2_equality_out, equality_3_equality_out, equality_4_equality_out,
       or_1_out, or_2_out;

  or or_1 (or_1_out, rs1[0], rs1[1], rs1[2], rs1[3], rs1[4]);
  or or_2 (or_2_out, rs2[0], rs2[1], rs2[2], rs2[3], rs2[4]);
  Equality equality_1 (.Input1(rs1), .Input2(rd_EX), .Equality_Out(equality_1_equality_out));
  Equality equality_2 (.Input1(rs1), .Input2(rd_MEM), .Equality_Out(equality_2_equality_out));
  Equality equality_3 (.Input1(rs2), .Input2(rd_EX), .Equality_Out(equality_3_equality_out));
  Equality equality_4 (.Input1(rs2), .Input2(rd_MEM), .Equality_Out(equality_4_equality_out));
  and and_1 (rs1_rdEX_EX, or_1_out, equality_1_equality_out, LW_EX);
  and and_2 (rs1_rdMEM_MEM, or_1_out, equality_2_equality_out, LW_EX);
  and and_3 (rs2_rdEX_EX, RType, equality_3_equality_out, or_2_out, LW_EX);
  and and_4 (rs2_rd2MEM_MEM, equality_4_equality_out, RType, or_2_out, LW_EX);
endmodule

module Equality (
  input  [4:0] Input1,
  input  [4:0] Input2,
  output Equality_Out
);

  wire xnor_1_out, xnor_2_out, xnor_3_out, xnor_4_out, xnor_5_out;

  xnor xnor_1 (xnor_1_out, Input1[0], Input2[0]);
  xnor xnor_2 (xnor_2_out, Input1[1], Input2[1]);
  xnor xnor_3 (xnor_3_out, Input1[2], Input2[2]);
  xnor xnor_4 (xnor_4_out, Input1[3], Input2[3]);
  xnor xnor_5 (xnor_5_out, Input1[4], Input2[4]);
  and and_1 (Equality_Out, xnor_1_out, xnor_2_out, xnor_3_out, xnor_4_out, xnor_5_out);
endmodule

module ALUinput_selection (
  input  ALUSrc,
  input  [31:0] B,
  input  [31:0] Immediate,
  input  [19:0] immU,
  input  UI,
  input  [31:0] A,
  input  [31:0] PC,
  input  [4:0] Sa_in,
  input  [4:0] rs2_Data,
  input  Shift,
  input  LUI,
  output [31:0] Bout,
  output [31:0] Aout,
  output [4:0] Sa_out
);

  wire [4:0] bit_extender_1_out, multiplexer_3_out;
  wire [31:0] bit_extender_2_out, multiplexer_1_out, multiplexer_2_out, reverse20to32_1_immuout;

  Multiplexer #(.width(32), .enable("false")) multiplexer_1 (
    .in0(B), .in1(Immediate), .out(multiplexer_1_out), .sel(ALUSrc));
  Multiplexer #(.width(32), .enable("false")) multiplexer_2 (.in0(A), .in1(PC), .out(multiplexer_2_out), .sel(UI));
  Multiplexer #(.width(5), .enable("false")) multiplexer_3 (
    .in0(Sa_in), .in1(rs2_Data), .out(multiplexer_3_out), .sel(Shift));
  assign bit_extender_1_out = {{4{1'b0}}, LUI};  // Bit_Extender bit_extender_1
  assign bit_extender_2_out = {{12{immU[19]}}, immU};  // Bit_Extender bit_extender_2
  Reverse20to32 reverse20to32_1 (.immU(immU), .immUout(reverse20to32_1_immuout));
  Multiplexer #(.width(32), .enable("false")) multiplexer_4 (
    .in0(multiplexer_1_out), .in1(reverse20to32_1_immuout), .out(Bout), .sel(UI));
  Multiplexer #(.width(32), .enable("false")) multiplexer_5 (
    .in0(multiplexer_2_out), .in1(bit_extender_2_out), .out(Aout), .sel(LUI));
  Multiplexer #(.width(5), .enable("false")) multiplexer_6 (
    .in0(multiplexer_3_out),
    .in1({bit_extender_1_out[1:0], bit_extender_1_out[0], bit_extender_1_out[3], bit_extender_1_out[4]}),
    .out(Sa_out), .sel(LUI));
endmodule

module Reverse20to32 (
  input  [19:0] immU,
  output [31:0] immUout
);

  assign {immUout[0], immUout[1], immUout[2], immUout[3], immUout[4], immUout[5], immUout[6], immUout[7], immUout[8], immUout[9], immUout[10], immUout[11], immUout[12], immUout[13], immUout[14], immUout[15], immUout[16], immUout[17], immUout[18], immUout[19], immUout[20], immUout[21], immUout[22], immUout[23], immUout[24], immUout[25], immUout[26], immUout[27], immUout[28], immUout[29], immUout[30], immUout[31]} = {{12{1'b0}}, {immU[0], immU[1], immU[2], immU[3], immU[4], immU[5], immU[6], immU[7], immU[8], immU[9], immU[10], immU[11], immU[12], immU[13], immU[14], immU[15], immU[16], immU[17], immU[18], immU[19]}};  // Bit_Extender bit_extender_1
endmodule
