// Logisim project Oscar.circ as structural Verilog
module Fetch (
  input  Clock,
  output [31:0] PC,
  output [31:0] Instruction
);

  wire [31:2] incrementer_1_p2;

  Register #(.width(32)) register_1 (.D({incrementer_1_p2, PC[1:0]}), .clk(Clock), .Q(PC));  // open: en, clr
  // Incrementer #(.width(30)) incrementer_1: pin names not known; wires that end beside it: PC[31:2], incrementer_1_p2, PC
  // RISC_VProgramROM risc_vprogramrom_1: pin names not known; wires that end beside it: Instruction
endmodule

module FetchRegister (
  input  [31:0] PCIn,
  input  [31:0] InstructionIn,
  input  Clock,
  output [31:0] PCOut,
  output [31:0] InstructionOut
);

  Register #(.width(32)) register_1 (.D(PCIn), .clk(Clock), .Q(PCOut));  // open: en, clr
  Register #(.width(32)) register_2 (.D(InstructionIn), .clk(Clock), .Q(InstructionOut));  // open: en, clr
endmodule

module Control (
  input  [6:0] Opcode,
  output ALUStuff,
  output RegisterOut,
  output Op0,
  output RType
);

  wire not_1_out, not_2_out, not_3_out;

  not not_1 (not_1_out, Opcode[0]);
  Multiplexer #(.select(2), .enable("false")) multiplexer_1 (
    .in0(Opcode[0]), .in1(Opcode[0]), .in2(not_1_out), .in3(Opcode[0]), .out(ALUStuff),
    .sel({Opcode[5], Opcode[2]}));
  not not_2 (not_2_out, Opcode[0]);
  Multiplexer #(.select(2), .enable("false")) multiplexer_2 (
    .in0(Opcode[0]), .in1(not_2_out), .in2(Opcode[0]), .in3(Opcode[0]), .sel({Opcode[5], Opcode[2]}));  // open: out
  not not_3 (not_3_out, Opcode[2]);
  and and_1 (RType, not_3_out, Opcode[5]);

  assign Op0 = Opcode[2];
  assign RegisterOut = Opcode[4];
endmodule
