// Logisim project P2.circ as structural Verilog: 21 circuits, main circuit RISCV
module RISCV (
);

  wire Clk_out, decode_1_alustuffout, decode_1_f3lsb, decode_1_luiout, decode_1_opmout, decode_1_opxout,
       decode_1_registerout, decode_1_rtype, decode_1_uiout, decoderegister_1_alustuffout,
       decoderegister_1_f3lsbout, decoderegister_1_luiout, decoderegister_1_opmout, decoderegister_1_opxout,
       decoderegister_1_registerout, decoderegister_1_rtypeout, decoderegister_1_uiout,
       execute_1_regwriteout, executeregister_1_regwriteout, memory_1_regwriteout,
       memoryregister_1_regwriteout;
  wire [3:0] decode_1_aluopout, decoderegister_1_aluopout;
  wire [4:0] decode_1_rd, decode_1_rs1, decode_1_rs2, decoderegister_1_rdout, decoderegister_1_rs1out,
       decoderegister_1_rs2out, execute_1_rwout, executeregister_1_rwout, hazards_1_sa, memory_1_rwout,
       memoryregister_1_rwout;
  wire [19:0] decode_1_immutype, decoderegister_1_immutypeout;
  wire [31:0] decode_1_aout, decode_1_bout, decode_1_immextended, decode_1_pcout, decoderegister_1_aout,
       decoderegister_1_bout, decoderegister_1_immextendedout, decoderegister_1_pcout, execute_1_aluoutput,
       execute_1_pcout, executeregister_1_alures_out, executeregister_1_pcout, fetch_1_instruction,
       fetch_1_pc, fetchregister_1_instructionout, fetchregister_1_pcout, hazards_1_aout, hazards_1_bout,
       memory_1_alures_out, memory_1_pcout, memoryregister_1_alures_out;

  Clock Clk (.out(Clk_out));
  Fetch fetch_1 (.Clock(Clk_out), .PC(fetch_1_pc), .Instruction(fetch_1_instruction));
  FetchRegister fetchregister_1 (
    .PCIn(fetch_1_pc), .InstructionIn(fetch_1_instruction), .Clock(Clk_out), .PCOut(fetchregister_1_pcout),
    .InstructionOut(fetchregister_1_instructionout));
  Decode decode_1 (
    .InstructionIn(fetchregister_1_instructionout), .WriteBack(memoryregister_1_alures_out), .Clock(Clk_out),
    .RegisterWE(memoryregister_1_regwriteout), .RegisterxW(memoryregister_1_rwout),
    .PCIn(fetchregister_1_pcout), .OpXOut(decode_1_opxout), .OpMOut(decode_1_opmout),
    .ALUStuffOut(decode_1_alustuffout), .RegisterOut(decode_1_registerout), .RType(decode_1_rtype),
    .LUIOut(decode_1_luiout), .UIOut(decode_1_uiout), .RD(decode_1_rd), .f3LSB(decode_1_f3lsb),
    .ALUOpOut(decode_1_aluopout), .RS1(decode_1_rs1), .RS2(decode_1_rs2), .ImmExtended(decode_1_immextended),
    .ImmUType(decode_1_immutype), .AOut(decode_1_aout), .BOut(decode_1_bout), .PCOut(decode_1_pcout));
  DecodeRegister decoderegister_1 (
    .OpXIn(decode_1_opxout), .OpMIn(decode_1_opmout), .ALUStuffIn(decode_1_alustuffout),
    .RegisterIn(decode_1_registerout), .RTypeIn(decode_1_rtype), .LUIIn(decode_1_luiout),
    .UIIn(decode_1_uiout), .RDIn(decode_1_rd), .f3LSBIn(decode_1_f3lsb), .ALUOpIn(decode_1_aluopout),
    .RS1In(decode_1_rs1), .RS2In(decode_1_rs2), .ImmExtendedIn(decode_1_immextended),
    .ImmUTypeIn(decode_1_immutype), .AIn(decode_1_aout), .BIn(decode_1_bout), .PCIn(decode_1_pcout),
    .Clock(Clk_out), .OpXOut(decoderegister_1_opxout), .OpMOut(decoderegister_1_opmout),
    .ALUStuffOut(decoderegister_1_alustuffout), .RegisterOut(decoderegister_1_registerout),
    .RTypeOut(decoderegister_1_rtypeout), .LUIOut(decoderegister_1_luiout), .UIOut(decoderegister_1_uiout),
    .RDOut(decoderegister_1_rdout), .f3LSBOut(decoderegister_1_f3lsbout),
    .ALUOpOut(decoderegister_1_aluopout), .RS1Out(decoderegister_1_rs1out), .RS2Out(decoderegister_1_rs2out),
    .ImmExtendedOut(decoderegister_1_immextendedout), .ImmUTypeOut(decoderegister_1_immutypeout),
    .AOut(decoderegister_1_aout), .BOut(decoderegister_1_bout), .PCOut(decoderegister_1_pcout));
  Hazards hazards_1 (
    .ALUSrc(decoderegister_1_alustuffout), .PC(decoderegister_1_pcout), .A(decoderegister_1_aout),
    .B(decoderegister_1_bout), .WriteBackData(executeregister_1_alures_out),
    .MemoryData(memoryregister_1_alures_out), .rs1(decoderegister_1_rs1out), .rs2(decoderegister_1_rs2out),
    .rd_EX(executeregister_1_rwout), .rd_MEM(memoryregister_1_rwout), .lw_EX(decoderegister_1_opxout),
    .lw_MEM(decoderegister_1_opmout), .RType(decoderegister_1_rtypeout),
    .ImmExtended32(decoderegister_1_immextendedout), .immUType(decoderegister_1_immutypeout),
    .UI(decoderegister_1_uiout), .LUI(decoderegister_1_luiout), .AOut(hazards_1_aout), .BOut(hazards_1_bout),
    .Sa(hazards_1_sa));
  Execute execute_1 (
    .A(hazards_1_aout), .B(hazards_1_bout), .f3b0(decoderegister_1_f3lsbout), .Sa(hazards_1_sa),
    .Op(decoderegister_1_aluopout), .RegWriteIn(decoderegister_1_registerout), .rW(decoderegister_1_rdout),
    .PC(decoderegister_1_pcout), .ALUOutput(execute_1_aluoutput), .RegWriteOut(execute_1_regwriteout),
    .rWout(execute_1_rwout), .PCout(execute_1_pcout));
  ExecuteRegister executeregister_1 (
    .ALUres_in(execute_1_aluoutput), .RegWrite(execute_1_regwriteout), .rW(execute_1_rwout),
    .PC(execute_1_pcout), .Clock(Clk_out), .ALUres_out(executeregister_1_alures_out),
    .RegWriteOut(executeregister_1_regwriteout), .rWout(executeregister_1_rwout),
    .PCout(executeregister_1_pcout));
  Memory memory_1 (
    .ALUres_in(executeregister_1_alures_out), .RegWriteIn(executeregister_1_regwriteout),
    .rW(executeregister_1_rwout), .PC(executeregister_1_pcout), .ALUres_out(memory_1_alures_out),
    .RegWriteOut(memory_1_regwriteout), .rWout(memory_1_rwout), .PCout(memory_1_pcout));
  MemoryRegister memoryregister_1 (
    .ALUres_in(memory_1_alures_out), .RegWriteIn(memory_1_regwriteout), .rW(memory_1_rwout),
    .PC(memory_1_pcout), .Clock(Clk_out), .ALUres_out(memoryregister_1_alures_out),
    .RegWriteOut(memoryregister_1_regwriteout), .rWout(memoryregister_1_rwout));  // open: PCout
endmodule

module Fetch (
  input  Clock,
  output [31:0] PC,
  output [31:0] Instruction
);

  wire [31:2] incrementer_1_p2;

  Register #(.width(32)) register_1 (.D({incrementer_1_p2, PC[1:0]}), .clk(Clock), .Q(PC));  // open: en, clr
  // Incrementer #(.width(30)) incrementer_1: pin names not known; wires that end beside it: PC[31:2], incrementer_1_p2, PC
  // RISC_VProgramROM risc_vprogramrom_1: pin names not known; wires that end beside it: Instruction

  // Notes on the sheet:
  //   contents of risc_vprogramrom_1 (hex, n*v repeats v):
  //   add t2, t0, t1 add t0, x0, t1 add t1, x0, t2 add t2, t0, t1 add t0, x0, t1 add t1, x0, t2 add t2,
  //   t0, t1 add t0, x0, t1 add t1, x0, t2 addi a0, t2, 0
endmodule

module Decode (
  input  [31:0] InstructionIn,
  input  [31:0] WriteBack,
  input  Clock,
  input  RegisterWE,
  input  [4:0] RegisterxW,
  input  [31:0] PCIn,
  output OpXOut,
  output OpMOut,
  output ALUStuffOut,
  output RegisterOut,
  output RType,
  output LUIOut,
  output UIOut,
  output [4:0] RD,
  output f3LSB,
  output [3:0] ALUOpOut,
  output [4:0] RS1,
  output [4:0] RS2,
  output [31:0] ImmExtended,
  output [19:0] ImmUType,
  output [31:0] AOut,
  output [31:0] BOut,
  output [31:0] PCOut
);

  wire not_1_out;

  // RegisterFile #(.trigger("falling")) registerfile_1: pin names not known; wires that end beside it: WriteBack, Clock, RegisterWE, RegisterxW, InstructionIn[19:15], InstructionIn[24:20], AOut, BOut
  assign ImmExtended = {{20{InstructionIn[31]}}, InstructionIn[31:20]};  // Bit_Extender bit_extender_1
  and and_1 (LUIOut, InstructionIn[2], InstructionIn[5]);
  and and_2 (UIOut, InstructionIn[2], not_1_out);
  not not_1 (not_1_out, InstructionIn[5]);
  OpcodeConverter opcodeconverter_1 (
    .f3(InstructionIn[14:12]), .f7B5(InstructionIn[30]), .RType(RType), .UI(InstructionIn[2]),
    .LUI(InstructionIn[5]), .ALUOpOut(ALUOpOut));
  OpcodeDeterminer opcodedeterminer_1 (.OpCodeIn(InstructionIn[6:0]), .OpXOut(OpXOut), .OpMOut(OpMOut));
  Control control_1 (.Opcode(InstructionIn[6:0]), .ALUStuff(ALUStuffOut), .RegisterOut(RegisterOut), .RType(RType));

  assign f3LSB = InstructionIn[12];
  assign ImmUType = InstructionIn[31:12];
  assign PCOut = PCIn;
  assign RD = InstructionIn[11:7];
  assign RS1 = InstructionIn[19:15];
  assign RS2 = InstructionIn[24:20];
endmodule

module FetchRegister (
  input  [31:0] PCIn,
  input  [31:0] InstructionIn,
  input  Clock,
  output [31:0] PCOut,
  output [31:0] InstructionOut
);

  Register #(.width(32)) register_1 (.D(PCIn), .clk(Clock), .Q(PCOut));  // open: en, clr
  Register #(.width(32)) register_2 (.D(InstructionIn), .clk(Clock), .Q(InstructionOut));  // open: en, clr
endmodule

module DecodeRegister (
  input  OpXIn,
  input  OpMIn,
  input  ALUStuffIn,
  input  RegisterIn,
  input  RTypeIn,
  input  LUIIn,
  input  UIIn,
  input  [4:0] RDIn,
  input  f3LSBIn,
  input  [3:0] ALUOpIn,
  input  [4:0] RS1In,
  input  [4:0] RS2In,
  input  [31:0] ImmExtendedIn,
  input  [19:0] ImmUTypeIn,
  input  [31:0] AIn,
  input  [31:0] BIn,
  input  [31:0] PCIn,
  input  Clock,
  output OpXOut,
  output OpMOut,
  output ALUStuffOut,
  output RegisterOut,
  output RTypeOut,
  output LUIOut,
  output UIOut,
  output [4:0] RDOut,
  output f3LSBOut,
  output [3:0] ALUOpOut,
  output [4:0] RS1Out,
  output [4:0] RS2Out,
  output [31:0] ImmExtendedOut,
  output [19:0] ImmUTypeOut,
  output [31:0] AOut,
  output [31:0] BOut,
  output [31:0] PCOut
);

  Register #(.width(1)) register_1 (.D(OpXIn), .clk(Clock), .Q(OpXOut));  // open: en, clr
  Register #(.width(1)) register_2 (.D(OpMIn), .clk(Clock), .Q(OpMOut));  // open: en, clr
  Register #(.width(1)) register_3 (.D(ALUStuffIn), .clk(Clock), .Q(ALUStuffOut));  // open: en, clr
  Register #(.width(1)) register_4 (.D(RegisterIn), .clk(Clock), .Q(RegisterOut));  // open: en, clr
  Register #(.width(1)) register_5 (.D(RTypeIn), .clk(Clock), .Q(RTypeOut));  // open: en, clr
  Register #(.width(1)) register_6 (.D(LUIIn), .clk(Clock), .Q(LUIOut));  // open: en, clr
  Register #(.width(1)) register_7 (.D(UIIn), .clk(Clock), .Q(UIOut));  // open: en, clr
  Register #(.width(5)) register_8 (.D(RDIn), .clk(Clock), .Q(RDOut));  // open: en, clr
  Register #(.width(1)) register_9 (.D(f3LSBIn), .clk(Clock), .Q(f3LSBOut));  // open: en, clr
  Register #(.width(4)) register_10 (.D(ALUOpIn), .clk(Clock), .Q(ALUOpOut));  // open: en, clr
  Register #(.width(5)) register_11 (.D(RS1In), .clk(Clock), .Q(RS1Out));  // open: en, clr
  Register #(.width(5)) register_12 (.D(RS2In), .clk(Clock), .Q(RS2Out));  // open: en, clr
  Register #(.width(32)) register_13 (.D(ImmExtendedIn), .clk(Clock), .Q(ImmExtendedOut));  // open: en, clr
  Register #(.width(20)) register_14 (.D(ImmUTypeIn), .clk(Clock), .Q(ImmUTypeOut));  // open: en, clr
  Register #(.width(32)) register_15 (.D(AIn), .clk(Clock), .Q(AOut));  // open: en, clr
  Register #(.width(32)) register_16 (.D(BIn), .clk(Clock), .Q(BOut));  // open: en, clr
  Register #(.width(32)) register_17 (.D(PCIn), .clk(Clock), .Q(PCOut));  // open: en, clr
endmodule

module Hazards (
  input  ALUSrc,
  input  [31:0] PC,
  input  [31:0] A,
  input  [31:0] B,
  input  [31:0] WriteBackData,
  input  [31:0] MemoryData,
  input  [4:0] rs1,
  input  [4:0] rs2,
  input  [4:0] rd_EX,
  input  [4:0] rd_MEM,
  input  lw_EX,
  input  lw_MEM,
  input  RType,
  input  [31:0] ImmExtended32,
  input  [19:0] immUType,
  input  UI,
  input  LUI,
  output [31:0] AOut,
  output [31:0] BOut,
  output [4:0] Sa
);

  wire hazarddetectionunit_1_rs1_rdex_ex, hazarddetectionunit_1_rs1_rdmem_mem,
       hazarddetectionunit_1_rs2_rd2mem_mem, hazarddetectionunit_1_rs2_rdex_ex;
  wire [31:0] forwardunit_1_aout, forwardunit_1_bout;

  HazardDetectionUnit hazarddetectionunit_1 (
    .rs1(rs1), .rs2(rs2), .rd_EX(rd_EX), .rd_MEM(rd_MEM), .LW_EX(lw_EX), .LW_MEM(lw_MEM), .RType(RType),
    .rs1_rdEX_EX(hazarddetectionunit_1_rs1_rdex_ex), .rs1_rdMEM_MEM(hazarddetectionunit_1_rs1_rdmem_mem),
    .rs2_rdEX_EX(hazarddetectionunit_1_rs2_rdex_ex), .rs2_rd2MEM_MEM(hazarddetectionunit_1_rs2_rd2mem_mem));
  ForwardUnit forwardunit_1 (
    .A(A), .B(B), .WriteBackData(WriteBackData), .MemoryData(MemoryData),
    .rs1_rdMEM_MEM(hazarddetectionunit_1_rs1_rdmem_mem),
    .rs2_rdMEM_MEM(hazarddetectionunit_1_rs2_rd2mem_mem), .rs1_rdEX_EX(hazarddetectionunit_1_rs1_rdex_ex),
    .rs2_rdEX_EX(hazarddetectionunit_1_rs2_rdex_ex), .Aout(forwardunit_1_aout), .Bout(forwardunit_1_bout));
  ALUinput_selection aluinput_selection_1 (
    .ALUSrc(ALUSrc), .B(forwardunit_1_bout), .Immediate(ImmExtended32), .immU(immUType), .UI(UI),
    .A(forwardunit_1_aout), .PC(PC), .Shift(RType), .LUI(LUI), .Bout(BOut), .Aout(AOut), .Sa_out(Sa));  // open: Sa_in, rs2_Data
endmodule

module Execute (
  input  [31:0] A,
  input  [31:0] B,
  input  f3b0,
  input  [4:0] Sa,
  input  [3:0] Op,
  input  RegWriteIn,
  input  [4:0] rW,
  input  [31:0] PC,
  output [31:0] ALUOutput,
  output RegWriteOut,
  output [4:0] rWout,
  output [31:0] PCout
);

  wire [31:0] alu_1_p6;

  // ALU alu_1: pin names not known; wires that end beside it: f3b0, A, B, Op, Sa, alu_1_p6
  ALUresult aluresult_1 (
    .A(A), .B(B), .C(alu_1_p6), .Funct30(f3b0), .Op0(Op[0]), .Op1(Op[1]), .RegWriteIn(RegWriteIn),
    .ALUOutput(ALUOutput), .RegWriteOut(RegWriteOut));

  assign PCout = PC;
  assign rWout = rW;
endmodule

module ExecuteRegister (
  input  [31:0] ALUres_in,
  input  RegWrite,
  input  [4:0] rW,
  input  [31:0] PC,
  input  Clock,
  output [31:0] ALUres_out,
  output RegWriteOut,
  output [4:0] rWout,
  output [31:0] PCout
);

  Register #(.width(32)) register_1 (.D(ALUres_in), .clk(Clock), .Q(ALUres_out));  // open: en, clr
  Register #(.width(1)) register_2 (.D(RegWrite), .clk(Clock), .Q(RegWriteOut));  // open: en, clr
  Register #(.width(5)) register_3 (.D(rW), .clk(Clock), .Q(rWout));  // open: en, clr
  Register #(.width(32)) register_4 (.D(PC), .clk(Clock), .Q(PCout));  // open: en, clr
endmodule

module Memory (
  input  [31:0] ALUres_in,
  input  RegWriteIn,
  input  [4:0] rW,
  input  [31:0] PC,
  output [31:0] ALUres_out,
  output RegWriteOut,
  output [4:0] rWout,
  output [31:0] PCout
);


  assign ALUres_out = ALUres_in;
  assign PCout = PC;
  assign RegWriteOut = RegWriteIn;
  assign rWout = rW;
endmodule

module MemoryRegister (
  input  [31:0] ALUres_in,
  input  RegWriteIn,
  input  [4:0] rW,
  input  [31:0] PC,
  input  Clock,
  output [31:0] ALUres_out,
  output RegWriteOut,
  output [4:0] rWout,
  output [31:0] PCout
);

  Register #(.width(32)) register_1 (.D(ALUres_in), .clk(Clock), .Q(ALUres_out));  // open: en, clr
  Register #(.width(1)) register_2 (.D(RegWriteIn), .clk(Clock), .Q(RegWriteOut));  // open: en, clr
  Register #(.width(5)) register_3 (.D(rW), .clk(Clock), .Q(rWout));  // open: en, clr
  Register #(.width(32)) register_4 (.D(PC), .clk(Clock), .Q(PCout));  // open: en, clr
endmodule

module Control (
  input  [6:0] Opcode,
  output ALUStuff,
  output RegisterOut,
  output RType
);

  wire not_1_out, not_2_out, not_3_out, not_4_out;

  not not_1 (not_1_out, Opcode[2]);
  not not_2 (not_2_out, Opcode[0]);
  not not_3 (not_3_out, Opcode[3]);
  not not_4 (not_4_out, Opcode[6]);
  Multiplexer #(.select(2), .enable("false")) multiplexer_1 (
    .in0(Opcode[0]), .in1(Opcode[0]), .in2(not_2_out), .in3(Opcode[0]), .out(ALUStuff),
    .sel({Opcode[5], Opcode[2]}));
  and and_1 (RType, Opcode[0], Opcode[1], not_1_out, not_3_out, Opcode[4], Opcode[5], not_4_out);

  assign RegisterOut = Opcode[4];
endmodule

module OpcodeConverter (
  input  [2:0] f3,
  input  f7B5,
  input  RType,
  input  UI,
  input  LUI,
  output [3:0] ALUOpOut
);

  wire and_1_out, and_2_out, and_3_out, and_4_out, and_5_out, and_6_out, and_7_out, and_8_out, not_1_out,
       not_2_out, not_3_out, not_4_out, not_5_out, not_6_out, not_7_out, not_8_out, not_9_out, not_10_out,
       not_11_out, not_12_out;

  not not_1 (not_1_out, f3[1]);
  not not_2 (not_2_out, f3[2]);
  not not_3 (not_3_out, f3[0]);
  not not_4 (not_4_out, f7B5);
  not not_5 (not_5_out, f3[0]);
  not not_6 (not_6_out, RType);
  not not_7 (not_7_out, f3[1]);
  not not_8 (not_8_out, f3[1]);
  not not_9 (not_9_out, f3[2]);
  not not_10 (not_10_out, f3[1]);
  not not_11 (not_11_out, f3[0]);
  not not_12 (not_12_out, f3[2]);
  and and_1 (and_1_out, not_1_out, f3[2], f7B5);
  or or_1 (ALUOpOut[0], and_1_out, and_2_out);
  and and_2 (and_2_out, f3[1], not_2_out);
  and and_3 (and_3_out, not_3_out, not_4_out);
  and and_4 (and_4_out, not_5_out, not_6_out);
  and and_5 (and_5_out, not_7_out, f3[2]);
  and and_6 (and_6_out, not_8_out, not_9_out);
  or or_2 (ALUOpOut[2], and_6_out, UI, and_7_out);
  and and_7 (and_7_out, f3[0], not_10_out);
  and and_8 (and_8_out, not_11_out, not_12_out);
  or or_3 (ALUOpOut[3], and_8_out, UI);
  or or_4 (ALUOpOut[1], and_3_out, and_4_out, UI, and_5_out);
endmodule

module OpcodeDeterminer (
  input  [6:0] OpCodeIn,
  output OpXOut,
  output OpMOut
);

  wire nor_1_out;

  nor nor_1 (nor_1_out, OpCodeIn[6], OpCodeIn[5], OpCodeIn[4], OpCodeIn[3], OpCodeIn[2]);
  and and_1 (OpMOut, nor_1_out, OpCodeIn[1], OpCodeIn[0]);
  not not_1 (OpXOut, OpMOut);
endmodule

module ALUresult (
  input  [31:0] A,
  input  [31:0] B,
  input  [31:0] C,
  input  Funct30,
  input  Op0,
  input  Op1,
  input  RegWriteIn,
  output [31:0] ALUOutput,
  output RegWriteOut
);

  wire comparator_1_lt, comparator_2_lt;
  wire [31:0] bit_extender_1_out, bit_extender_2_out, multiplexer_1_out, multiplexer_2_out;

  Comparator #(.width(32)) comparator_1 (.a(A), .b(B), .lt(comparator_1_lt));  // open: gt, eq
  Comparator #(.width(32), .mode("unsigned")) comparator_2 (.a(A), .b(B), .lt(comparator_2_lt));  // open: gt, eq
  assign bit_extender_1_out = {{31{1'b0}}, comparator_1_lt};  // Bit_Extender bit_extender_1
  assign bit_extender_2_out = {{31{1'b0}}, comparator_2_lt};  // Bit_Extender bit_extender_2
  Multiplexer #(.width(32), .enable("false")) multiplexer_1 (
    .in0(bit_extender_1_out), .in1(bit_extender_2_out), .out(multiplexer_1_out), .sel(Funct30));
  Multiplexer #(.width(32), .enable("false")) multiplexer_2 (
    .in0(multiplexer_1_out), .in1(C), .out(multiplexer_2_out), .sel(Op0));
  Multiplexer #(.width(32), .enable("false")) multiplexer_3 (
    .in0(multiplexer_2_out), .in1(C), .out(ALUOutput), .sel(Op1));

  assign RegWriteOut = RegWriteIn;
endmodule

module Equality (
  input  [4:0] Input1,
  input  [4:0] Input2,
  output Equality_Out
);

  wire xnor_1_out, xnor_2_out, xnor_3_out, xnor_4_out, xnor_5_out;

  xnor xnor_1 (xnor_1_out, Input1[0], Input2[0]);
  xnor xnor_2 (xnor_2_out, Input1[1], Input2[1]);
  xnor xnor_3 (xnor_3_out, Input1[2], Input2[2]);
  xnor xnor_4 (xnor_4_out, Input1[3], Input2[3]);
  xnor xnor_5 (xnor_5_out, Input1[4], Input2[4]);
  and and_1 (Equality_Out, xnor_1_out, xnor_2_out, xnor_3_out, xnor_4_out, xnor_5_out);
endmodule

module ALUinput_selection (
  input  ALUSrc,
  input  [31:0] B,
  input  [31:0] Immediate,
  input  [19:0] immU,
  input  UI,
  input  [31:0] A,
  input  [31:0] PC,
  input  [4:0] Sa_in,
  input  [4:0] rs2_Data,
  input  Shift,
  input  LUI,
  output [31:0] Bout,
  output [31:0] Aout,
  output [4:0] Sa_out
);

  wire [4:0] bit_extender_1_out, multiplexer_3_out;
  wire [31:0] bit_extender_2_out, bit_extender_3_out, multiplexer_1_out, multiplexer_2_out;

  Multiplexer #(.width(32), .enable("false")) multiplexer_1 (
    .in0(B), .in1(Immediate), .out(multiplexer_1_out), .sel(ALUSrc));
  Multiplexer #(.width(32), .enable("false")) multiplexer_2 (.in0(A), .in1(PC), .out(multiplexer_2_out), .sel(UI));
  Multiplexer #(.width(5), .enable("false")) multiplexer_3 (
    .in0(Sa_in), .in1(rs2_Data), .out(multiplexer_3_out), .sel(Shift));
  assign bit_extender_1_out = {{4{1'b0}}, LUI};  // Bit_Extender bit_extender_1
  assign bit_extender_2_out = {{12{immU[19]}}, immU};  // Bit_Extender bit_extender_2
  assign bit_extender_3_out = {{12{1'b0}}, {immU[0], immU[1], immU[2], immU[3], immU[4], immU[5], immU[6], immU[7], immU[8], immU[9], immU[10], immU[11], immU[12], immU[13], immU[14], immU[15], immU[16], immU[17], immU[18], immU[19]}};  // Bit_Extender bit_extender_3
  Multiplexer #(.width(32), .enable("false")) multiplexer_4 (
    .in0(multiplexer_1_out),
    .in1({bit_extender_3_out[0], bit_extender_3_out[1], bit_extender_3_out[2], bit_extender_3_out[3], bit_extender_3_out[4], bit_extender_3_out[5], bit_extender_3_out[6], bit_extender_3_out[7], bit_extender_3_out[8], bit_extender_3_out[9], bit_extender_3_out[10], bit_extender_3_out[11], bit_extender_3_out[12], bit_extender_3_out[13], bit_extender_3_out[14], bit_extender_3_out[15], bit_extender_3_out[16], bit_extender_3_out[17], bit_extender_3_out[18], bit_extender_3_out[19], bit_extender_3_out[20], bit_extender_3_out[21], bit_extender_3_out[22], bit_extender_3_out[23], bit_extender_3_out[24], bit_extender_3_out[25], bit_extender_3_out[26], bit_extender_3_out[27], bit_extender_3_out[28], bit_extender_3_out[29], bit_extender_3_out[30], bit_extender_3_out[31]}),
    .out(Bout), .sel(UI));
  Multiplexer #(.width(32), .enable("false")) multiplexer_5 (
    .in0(multiplexer_2_out), .in1(bit_extender_2_out), .out(Aout), .sel(LUI));
  Multiplexer #(.width(5), .enable("false")) multiplexer_6 (
    .in0(multiplexer_3_out),
    .in1({bit_extender_1_out[1:0], bit_extender_1_out[0], bit_extender_1_out[3], bit_extender_1_out[4]}),
    .out(Sa_out), .sel(LUI));
endmodule

module HazardDetectionUnit (
  input  [4:0] rs1,
  input  [4:0] rs2,
  input  [4:0] rd_EX,
  input  [4:0] rd_MEM,
  input  LW_EX,
  input  LW_MEM,
  input  RType,
  output rs1_rdEX_EX,
  output rs1_rdMEM_MEM,
  output rs2_rdEX_EX,
  output rs2_rd2MEM_MEM
);

  wire equality_1_equality_out, equality_2_equality_out, equality_3_equality_out, equality_4_equality_out,
       or_1_out, or_2_out;

  or or_1 (or_1_out, rs1[0], rs1[1], rs1[2], rs1[3], rs1[4]);
  or or_2 (or_2_out, rs2[0], rs2[1], rs2[2], rs2[3], rs2[4]);
  Equality equality_1 (.Input1(rs1), .Input2(rd_EX), .Equality_Out(equality_1_equality_out));
  Equality equality_2 (.Input1(rs1), .Input2(rd_MEM), .Equality_Out(equality_2_equality_out));
  Equality equality_3 (.Input1(rs2), .Input2(rd_EX), .Equality_Out(equality_3_equality_out));
  Equality equality_4 (.Input1(rs2), .Input2(rd_MEM), .Equality_Out(equality_4_equality_out));
  and and_1 (rs1_rdEX_EX, or_1_out, equality_1_equality_out, LW_EX);
  and and_2 (rs1_rdMEM_MEM, or_1_out, equality_2_equality_out, LW_EX);
  and and_3 (rs2_rdEX_EX, equality_3_equality_out, RType, or_2_out, LW_EX);
  and and_4 (rs2_rd2MEM_MEM, equality_4_equality_out, RType, or_2_out, LW_EX);
endmodule

module ForwardUnit (
  input  [31:0] A,
  input  [31:0] B,
  input  [31:0] WriteBackData,
  input  [31:0] MemoryData,
  input  rs1_rdMEM_MEM,
  input  rs2_rdMEM_MEM,
  input  rs1_rdEX_EX,
  input  rs2_rdEX_EX,
  output [31:0] Aout,
  output [31:0] Bout
);

  wire [31:0] multiplexer_1_out, multiplexer_2_out;

  Multiplexer #(.width(32), .enable("false")) multiplexer_1 (
    .in0(A), .in1(MemoryData), .out(multiplexer_1_out), .sel(rs1_rdMEM_MEM));
  Multiplexer #(.width(32), .enable("false")) multiplexer_2 (
    .in0(B), .in1(MemoryData), .out(multiplexer_2_out), .sel(rs2_rdMEM_MEM));
  Multiplexer #(.width(32), .enable("false")) multiplexer_3 (
    .in0(multiplexer_1_out), .in1(WriteBackData), .out(Aout), .sel(rs1_rdEX_EX));
  Multiplexer #(.width(32), .enable("false")) multiplexer_4 (
    .in0(multiplexer_2_out), .in1(WriteBackData), .out(Bout), .sel(rs2_rdEX_EX));
endmodule

module OpcodeConverterBackup (
  input  [2:0] f3,
  input  f7b5,
  input  rtype,
  input  ui,
  input  lui,
  output [3:0] opcode
);

  wire and_1_out, and_2_out, and_3_out, and_4_out, and_5_out, and_6_out, and_7_out, and_8_out, and_9_out,
       and_10_out, not_1_out, not_2_out, not_3_out, not_4_out, not_5_out, not_6_out, not_7_out, not_8_out,
       not_9_out, not_10_out, not_11_out;
  wire [2:0] not_13_out;
  wire [2:2] not_14_out;
  wire [3:0] multiplexer_1_out, or_4_out;

  not not_1 (not_1_out, f3[2]);
  and and_1 (and_1_out, not_1_out, not_2_out);
  not not_2 (not_2_out, f3[1]);
  not not_3 (not_3_out, f3[1]);
  and and_2 (and_2_out, not_3_out, f3[0]);
  and and_3 (and_3_out, f3[0], not_4_out);
  not not_4 (not_4_out, f3[1]);
  and and_4 (and_4_out, f3[0], f3[2]);
  and and_5 (and_5_out, f3[2], not_5_out);
  not not_5 (not_5_out, f3[1]);
  not not_6 (not_6_out, f3[1]);
  and and_6 (and_6_out, not_6_out, f3[2]);
  not not_7 (not_7_out, f3[0]);
  and and_7 (and_7_out, f7b5, not_7_out, not_8_out, rtype);
  not not_8 (not_8_out, f3[1]);
  and and_8 (and_8_out, f7b5, not_9_out);
  not not_9 (not_9_out, f3[1]);
  not not_10 (not_10_out, f3[1]);
  and and_9 (and_9_out, not_10_out, not_11_out);
  not not_11 (not_11_out, f3[0]);
  and and_10 (and_10_out, f3[2], f3[1]);
  or or_1 (or_4_out[3], and_1_out, and_2_out);
  or or_2 (or_4_out[1], and_3_out, and_4_out, and_5_out);
  or or_3 (or_4_out[2], and_6_out, and_7_out);
  or or_4 (or_4_out[0], and_8_out, and_9_out, and_10_out);
  not not_12 (not_13_out[2], lui);
  not not_13 (not_13_out[0], lui);
  not not_14 (not_14_out[2], ui);
  Multiplexer #(.width(4), .enable("false")) multiplexer_1 (
    .in0({ui, {2{not_14_out[2]}}, ui}), .in1({lui, not_13_out[2], lui, not_13_out[0]}),
    .out(multiplexer_1_out), .sel(lui));
  Multiplexer #(.width(4), .enable("false")) multiplexer_2 (
    .in0(or_4_out), .in1(multiplexer_1_out), .out(opcode), .sel(ui));
endmodule

module OpcodeConverterTesting (
  input  f3b0,
  input  f3b1,
  input  f3b2,
  input  f7b5,
  input  rtype,
  input  ui2,
  input  lui5,
  output ALU0,
  output ALU1,
  output ALU2,
  output ALU3
);

  wire and_1_out, and_2_out, and_3_out, and_4_out, and_5_out, and_6_out, and_7_out, and_8_out, not_1_out,
       not_2_out, not_3_out, not_4_out, not_5_out, not_6_out, not_7_out, not_8_out, not_9_out, not_10_out,
       not_11_out, not_12_out;

  not not_1 (not_1_out, f3b1);
  not not_2 (not_2_out, f3b2);
  not not_3 (not_3_out, f3b0);
  not not_4 (not_4_out, f7b5);
  not not_5 (not_5_out, f3b0);
  not not_6 (not_6_out, rtype);
  not not_7 (not_7_out, f3b1);
  not not_8 (not_8_out, f3b1);
  not not_9 (not_9_out, f3b2);
  not not_10 (not_10_out, f3b1);
  not not_11 (not_11_out, f3b0);
  not not_12 (not_12_out, f3b2);
  and and_1 (and_1_out, not_1_out, f3b2, f7b5);
  or or_1 (ALU0, and_1_out, and_2_out);
  and and_2 (and_2_out, f3b1, not_2_out);
  and and_3 (and_3_out, not_3_out, not_4_out);
  and and_4 (and_4_out, not_5_out, not_6_out);
  and and_5 (and_5_out, not_7_out, f3b2);
  and and_6 (and_6_out, not_8_out, not_9_out);
  or or_2 (ALU2, and_6_out, ui2, and_7_out);
  and and_7 (and_7_out, f3b0, not_10_out);
  and and_8 (and_8_out, not_11_out, not_12_out);
  or or_3 (ALU3, and_8_out, ui2);
  or or_4 (ALU1, and_3_out, and_4_out, ui2, and_5_out);
endmodule

module Trial (
);

  wire clock_1_out, decode_1_alustuffout, decode_1_f3lsb, decode_1_luiout, decode_1_opmout, decode_1_opxout,
       decode_1_registerout, decode_1_rtype, decode_1_uiout, decoderegister_1_alustuffout,
       decoderegister_1_f3lsbout, decoderegister_1_luiout, decoderegister_1_opmout, decoderegister_1_opxout,
       decoderegister_1_registerout, decoderegister_1_rtypeout, decoderegister_1_uiout,
       execute_1_regwriteout, executeregister_1_regwriteout, memory_1_regwriteout,
       memoryregister_1_regwriteout, memoryregister_2_regwriteout;
  wire [3:0] decode_1_aluopout, decoderegister_1_aluopout;
  wire [4:0] decode_1_rd, decode_1_rs1, decode_1_rs2, decoderegister_1_rdout, decoderegister_1_rs1out,
       decoderegister_1_rs2out, execute_1_rwout, executeregister_1_rwout, hazards_1_sa, memory_1_rwout,
       memoryregister_1_rwout, memoryregister_2_rwout;
  wire [19:0] decode_1_immutype, decoderegister_1_immutypeout;
  wire [31:0] decode_1_aout, decode_1_bout, decode_1_immextended, decode_1_pcout, decoderegister_1_aout,
       decoderegister_1_bout, decoderegister_1_immextendedout, decoderegister_1_pcout, execute_1_aluoutput,
       execute_1_pcout, executeregister_1_alures_out, executeregister_1_pcout, fetch_1_instruction,
       fetch_1_pc, fetchregister_1_instructionout, fetchregister_1_pcout, hazards_1_aout, hazards_1_bout,
       memory_1_alures_out, memory_1_pcout, memoryregister_1_alures_out, memoryregister_1_pcout,
       memoryregister_2_alures_out;

  Clock clock_1 (.out(clock_1_out));
  Fetch fetch_1 (.Clock(clock_1_out), .PC(fetch_1_pc), .Instruction(fetch_1_instruction));
  FetchRegister fetchregister_1 (
    .PCIn(fetch_1_pc), .InstructionIn(fetch_1_instruction), .Clock(clock_1_out),
    .PCOut(fetchregister_1_pcout), .InstructionOut(fetchregister_1_instructionout));
  Decode decode_1 (
    .InstructionIn(fetchregister_1_instructionout), .WriteBack(memoryregister_2_alures_out),
    .Clock(clock_1_out), .RegisterWE(memoryregister_2_regwriteout), .RegisterxW(memoryregister_2_rwout),
    .PCIn(fetchregister_1_pcout), .OpXOut(decode_1_opxout), .OpMOut(decode_1_opmout),
    .ALUStuffOut(decode_1_alustuffout), .RegisterOut(decode_1_registerout), .RType(decode_1_rtype),
    .LUIOut(decode_1_luiout), .UIOut(decode_1_uiout), .RD(decode_1_rd), .f3LSB(decode_1_f3lsb),
    .ALUOpOut(decode_1_aluopout), .RS1(decode_1_rs1), .RS2(decode_1_rs2), .ImmExtended(decode_1_immextended),
    .ImmUType(decode_1_immutype), .AOut(decode_1_aout), .BOut(decode_1_bout), .PCOut(decode_1_pcout));
  DecodeRegister decoderegister_1 (
    .OpXIn(decode_1_opxout), .OpMIn(decode_1_opmout), .ALUStuffIn(decode_1_alustuffout),
    .RegisterIn(decode_1_registerout), .RTypeIn(decode_1_rtype), .LUIIn(decode_1_luiout),
    .UIIn(decode_1_uiout), .RDIn(decode_1_rd), .f3LSBIn(decode_1_f3lsb), .ALUOpIn(decode_1_aluopout),
    .RS1In(decode_1_rs1), .RS2In(decode_1_rs2), .ImmExtendedIn(decode_1_immextended),
    .ImmUTypeIn(decode_1_immutype), .AIn(decode_1_aout), .BIn(decode_1_bout), .PCIn(decode_1_pcout),
    .Clock(clock_1_out), .OpXOut(decoderegister_1_opxout), .OpMOut(decoderegister_1_opmout),
    .ALUStuffOut(decoderegister_1_alustuffout), .RegisterOut(decoderegister_1_registerout),
    .RTypeOut(decoderegister_1_rtypeout), .LUIOut(decoderegister_1_luiout), .UIOut(decoderegister_1_uiout),
    .RDOut(decoderegister_1_rdout), .f3LSBOut(decoderegister_1_f3lsbout),
    .ALUOpOut(decoderegister_1_aluopout), .RS1Out(decoderegister_1_rs1out), .RS2Out(decoderegister_1_rs2out),
    .ImmExtendedOut(decoderegister_1_immextendedout), .ImmUTypeOut(decoderegister_1_immutypeout),
    .AOut(decoderegister_1_aout), .BOut(decoderegister_1_bout), .PCOut(decoderegister_1_pcout));
  Hazards hazards_1 (
    .ALUSrc(decoderegister_1_alustuffout), .PC(decoderegister_1_pcout), .A(decoderegister_1_aout),
    .B(decoderegister_1_bout), .WriteBackData(executeregister_1_alures_out),
    .MemoryData(memoryregister_2_alures_out), .rs1(decoderegister_1_rs1out), .rs2(decoderegister_1_rs2out),
    .rd_EX(executeregister_1_rwout), .rd_MEM(memoryregister_2_rwout), .lw_EX(decoderegister_1_opxout),
    .lw_MEM(decoderegister_1_opmout), .RType(decoderegister_1_rtypeout),
    .ImmExtended32(decoderegister_1_immextendedout), .immUType(decoderegister_1_immutypeout),
    .UI(decoderegister_1_uiout), .LUI(decoderegister_1_luiout), .AOut(hazards_1_aout), .BOut(hazards_1_bout),
    .Sa(hazards_1_sa));
  Execute execute_1 (
    .A(hazards_1_aout), .B(hazards_1_bout), .f3b0(decoderegister_1_f3lsbout), .Sa(hazards_1_sa),
    .Op(decoderegister_1_aluopout), .RegWriteIn(decoderegister_1_registerout), .rW(decoderegister_1_rdout),
    .PC(decoderegister_1_pcout), .ALUOutput(execute_1_aluoutput), .RegWriteOut(execute_1_regwriteout),
    .rWout(execute_1_rwout), .PCout(execute_1_pcout));
  ExecuteRegister executeregister_1 (
    .ALUres_in(execute_1_aluoutput), .RegWrite(execute_1_regwriteout), .rW(execute_1_rwout),
    .PC(execute_1_pcout), .Clock(clock_1_out), .ALUres_out(executeregister_1_alures_out),
    .RegWriteOut(executeregister_1_regwriteout), .rWout(executeregister_1_rwout),
    .PCout(executeregister_1_pcout));
  Memory memory_1 (
    .ALUres_in(executeregister_1_alures_out), .RegWriteIn(executeregister_1_regwriteout),
    .rW(executeregister_1_rwout), .PC(executeregister_1_pcout), .ALUres_out(memory_1_alures_out),
    .RegWriteOut(memory_1_regwriteout), .rWout(memory_1_rwout), .PCout(memory_1_pcout));
  MemoryRegister memoryregister_1 (
    .ALUres_in(memory_1_alures_out), .RegWriteIn(memory_1_regwriteout), .rW(memory_1_rwout),
    .PC(memory_1_pcout), .Clock(clock_1_out), .ALUres_out(memoryregister_1_alures_out),
    .RegWriteOut(memoryregister_1_regwriteout), .rWout(memoryregister_1_rwout), .PCout(memoryregister_1_pcout));
  MemoryRegister memoryregister_2 (
    .ALUres_in(memoryregister_1_alures_out), .RegWriteIn(memoryregister_1_regwriteout),
    .rW(memoryregister_1_rwout), .PC(memoryregister_1_pcout), .Clock(clock_1_out),
    .ALUres_out(memoryregister_2_alures_out), .RegWriteOut(memoryregister_2_regwriteout),
    .rWout(memoryregister_2_rwout));  // open: PCout
endmodule
